// Digital circuit ram_banking_4.dig as structural Verilog
module ram_banking_4 (
  input  in_1,
  input  in_2,
  input  in_3,
  output out_4
);

  wire _74273_1_p4, _74273_1_p5, _74273_1_p6, _74273_1_p7, _74273_1_p8, _74273_1_p9, _74273_1_p10;

  // _74273 _74273_1: pin names not known; wires that end beside it: in_1, in_2, in_3, _74273_1_p4, _74273_1_p5, _74273_1_p6, _74273_1_p7, _74273_1_p8, _74273_1_p9, _74273_1_p10, 1'b1, 1'b0, out_4
  // NotConnected on _74273_1_p4
  // NotConnected on _74273_1_p5
  // NotConnected on _74273_1_p6
  // NotConnected on _74273_1_p7
  // NotConnected on _74273_1_p8
  // NotConnected on _74273_1_p9
  // NotConnected on _74273_1_p10

  // Notes on the sheet:
  //   in_2: default 1
endmodule
