// Digital circuit rom_banking_2.dig as structural Verilog
module rom_banking_2 (
  input  \Ф2 ,
  input  RES,
  input  in_4,
  input  in_5,
  input  in_6,
  input  in_7,
  input  in_8,
  input  in_9,
  input  in_10,
  input  in_11,
  input  EN,
  output out_1,
  output out_13,
  output out_14,
  output out_15,
  output out_16,
  output out_17,
  output out_18,
  output out_19
);

  wire nand_1_out, not_1_out;

  not not_1 (not_1_out, EN);
  nand nand_1 (nand_1_out, \Ф2 , not_1_out);
  // _74273 _74273_1: pin names not known; wires that end beside it: nand_1_out, RES, in_4, in_5, in_6, in_7, in_8, in_9, in_10, in_11, 1'b1, 1'b0, out_1, out_13, out_14, out_15, out_16, out_17, out_18, out_19

  // Notes on the sheet:
  //   RES: default 1
  //   EN: default 1
endmodule
